# Fritzing sketch capacitor (saved by Fritzing 0.8.7b)
breadboards: 1

parts:
  Part1 = Arduino Uno (Rev3)
  R1 = Resistor [tolerance=±5% resistance=10k package=THT]
  C = Ceramic Capacitor [package="100 mil [THT, multilayer]"]
  R2 = Resistor [tolerance=±5% resistance=220 package=THT]
  LED1 = LED - 5mm [color="Green (560nm)" package="5 mm [THT]"]
  LED2 = LED - 5mm [color="Red (660nm)" package="5 mm [THT]"]
  Q1 = NPN-Transistor [part_number=BC547 package="TO92 [THT]"]
  R3 = Resistor [tolerance=±5% resistance=220 package=THT]
  R4 = Resistor [tolerance=±5% resistance=10k package=THT]
  R5 = Resistor [tolerance=±5% resistance=1k package=THT]

nets:
  A0: Part1.A0, R1.Pin_1, C.1, R2.Pin_1
  N1: Part1.D11_PWM/MOSI, LED1.anode, R4.Pin_0
  N2: Part1.D12/MISO, R2.Pin_0
  N3: Part1.D13/SCK, R1.Pin_0
  GND: Part1.GND, C.0, LED2.cathode, Q1.E, R3.Pin_0
  5V: Part1.5V, R5.Pin_0
  N4: LED1.cathode, R3.Pin_1
  N5: LED2.anode, Q1.C, R5.Pin_1
  N6: Q1.B, R4.Pin_1
