# Fritzing sketch counter (saved by Fritzing 0.8.7b)
breadboards: 1

parts:
  Part1 = Arduino Uno (Rev3)
  LED1 = LED - 5mm [color="Red (633nm)" package="5 mm [THT]"]
  LED2 = LED - 5mm [color="Red (633nm)" package="5 mm [THT]"]
  LED3 = LED - 5mm [color="Red (633nm)" package="5 mm [THT]"]
  R1 = Resistor [tolerance=±5% resistance=220 package=THT]
  R2 = Resistor [tolerance=±5% resistance=10k package=THT]
  S1 = Pushbutton [package="[THT]"]

nets:
  N1: Part1.D10_PWM/SS, R2.Pin_0, S1.Pin_1, S1.Pin_2
  N2: Part1.D11_PWM/MOSI, LED3.anode
  N3: Part1.D12/MISO, LED2.anode
  N4: Part1.D13/SCK, LED1.anode
  GND: Part1.GND, R1.Pin_1, R2.Pin_1
  5V: Part1.5V, S1.Pin_3, S1.Pin_4
  N5: LED1.cathode, LED2.cathode, LED3.cathode, R1.Pin_0
