# Fritzing sketch debounce (saved by Fritzing 0.8.7b)
breadboards: 1

parts:
  Part1 = Arduino Uno (Rev3)
  LED1 = LED - 5mm [color="Red (633nm)" package="5 mm [THT]"]
  R1 = Resistor [tolerance=±5% resistance=220 package=THT]
  R2 = Resistor [tolerance=±5% resistance=10k package=THT]
  S1 = Pushbutton [package="[THT]"]

nets:
  N1: Part1.D12/MISO, R2.Pin_0, S1.Pin_3, S1.Pin_4
  N2: Part1.D13/SCK, LED1.anode
  5V: Part1.5V, S1.Pin_1, S1.Pin_2
  GND: Part1.GND, R1.Pin_1, R2.Pin_1
  N3: LED1.cathode, R1.Pin_0
